# Fritzing sketch LED-BAR Graph (saved by Fritzing 0.9.3b)
breadboards: 1

parts:
  D1 = LED_BARGRAPH_10 [package=led_bargaph_10]
  Part1 = Arduino Uno (Rev3)
  R1 = Resistor [tolerance=±5% resistance=470 package=THT]
  R2 = Resistor [tolerance=±5% resistance=470 package=THT]
  R3 = Resistor [tolerance=±5% resistance=470 package=THT]
  R4 = Resistor [tolerance=±5% resistance=470 package=THT]
  R5 = Resistor [tolerance=±5% resistance=470 package=THT]
  R6 = Resistor [tolerance=±5% resistance=470 package=THT]
  R7 = Resistor [tolerance=±5% resistance=470 package=THT]
  R8 = Resistor [tolerance=±5% resistance=470 package=THT]
  R9 = Resistor [tolerance=±5% resistance=470 package=THT]
  R10 = Resistor [tolerance=±5% resistance=470 package=THT]

nets:
  N1: D1.A_A, Part1.D11_PWM/MOSI
  N2: D1.B_A, Part1.D10_PWM/SS
  N3: D1.C_A, Part1.D9_PWM
  N4: D1.D_A, Part1.D8
  N5: D1.E_A, Part1.D7
  N6: D1.F_A, Part1.D6_PWM
  N7: D1.G_A, Part1.D5_PWM
  N8: D1.H_A, Part1.D4
  N9: D1.I_A, Part1.D3_PWM
  N10: D1.J_A, Part1.D2
  N11: D1.J_C, R9.Pin_0
  N12: D1.I_C, R8.Pin_0
  N13: D1.H_C, R7.Pin_0
  N14: D1.G_C, R6.Pin_0
  N15: D1.F_C, R5.Pin_0
  N16: D1.E_C, R10.Pin_0
  N17: D1.D_C, R4.Pin_0
  N18: D1.C_C, R3.Pin_0
  N19: D1.B_C, R2.Pin_0
  N20: D1.A_C, R1.Pin_0
  N21: Part1.GND, R1.Pin_1, R2.Pin_1, R3.Pin_1, R4.Pin_1, R5.Pin_1, R6.Pin_1, R7.Pin_1, R8.Pin_1, R9.Pin_1, R10.Pin_1
