# Fritzing sketch Piezo Buzzer Piano (saved by Fritzing 0.9.3b)
breadboards: 1

parts:
  Part1 = Arduino Uno (Rev3)
  S1 = Pushbutton [package="[SMD]"]
  S2 = Pushbutton [package="[SMD]"]
  S3 = Pushbutton [package="[SMD]"]
  S4 = Pushbutton [package="[SMD]"]
  S5 = Pushbutton [package="[SMD]"]
  S6 = Pushbutton [package="[SMD]"]
  S7 = Pushbutton [package="[SMD]"]
  S8 = Pushbutton [package="[SMD]"]
  R2 = Resistor [tolerance=±5% resistance=220 package=THT]
  R3 = Resistor [tolerance=±5% resistance=220 package=THT]
  R4 = Resistor [tolerance=±5% resistance=220 package=THT]
  R5 = Resistor [tolerance=±5% resistance=220 package=THT]
  R6 = Resistor [tolerance=±5% resistance=220 package=THT]
  R7 = Resistor [tolerance=±5% resistance=220 package=THT]
  R8 = Resistor [tolerance=±5% resistance=220 package=THT]
  R9 = Resistor [tolerance=±5% resistance=220 package=THT]
  J1 = Piezo Speaker

nets:
  N1: Part1.D8, S7.Pin_1, S7.Pin_2, R8.Pin_1
  N2: Part1.D9_PWM, S6.Pin_1, S6.Pin_2, R9.Pin_1
  N3: Part1.D13/SCK, J1.pin2
  N4: Part1.GND, S1.Pin_3, S1.Pin_4, S2.Pin_3, S2.Pin_4, S3.Pin_3, S3.Pin_4, S4.Pin_3, S4.Pin_4, S5.Pin_3, S5.Pin_4, S6.Pin_3, S6.Pin_4, S7.Pin_3, S7.Pin_4, S8.Pin_3, S8.Pin_4, J1.pin1
  N5: Part1.D2, S1.Pin_1, S1.Pin_2, R2.Pin_0
  N6: Part1.D3_PWM, S2.Pin_1, S2.Pin_2, R3.Pin_1
  N7: Part1.D4, S3.Pin_1, S3.Pin_2, R4.Pin_1
  N8: Part1.D5_PWM, S4.Pin_1, S4.Pin_2, R5.Pin_1
  N9: Part1.D6_PWM, S5.Pin_1, S5.Pin_2, R6.Pin_1
  N10: Part1.D7, S8.Pin_1, S8.Pin_2, R7.Pin_1
  N11: Part1.5V, R2.Pin_1, R3.Pin_0, R4.Pin_0, R5.Pin_0, R6.Pin_0, R7.Pin_0, R8.Pin_0, R9.Pin_0
