# Fritzing sketch Sound Sensor (saved by Fritzing 0.9.3b)

parts:
  Part1 = Breakout Board for Electret Microphone
  Part2 = Arduino Uno (Rev3)

nets:
  VCC: Part1.VCC, Part2.5V
  GND: Part1.GND, Part2.GND
  N1: Part1.AUD, Part2.D2
