# Fritzing sketch PWMDC (saved by Fritzing 0.9.3b)
breadboards: 1

parts:
  Part1 = Arduino Uno (Rev3)
  M1 = DC Motor
  Q1 = TRANSISTOR_NPN [package=to-92-ammo]
  R1 = Resistor [tolerance=±5% resistance=270 package=THT]
  D1 = Rectifier Diode [part_number=1N4001 package="300 mil [THT]"]

nets:
  N1: Part1.D3_PWM, R1.Pin_1
  N2: Part1.5V, M1.pin_1, D1.cathode
  N3: Part1.GND, Q1.E
  N4: M1.pin_2, Q1.C, D1.anode
  N5: Q1.B, R1.Pin_0
