# Fritzing sketch Untitled Sketch (saved by Fritzing 0.9.3b)
breadboards: 1

parts:
  IR1 = TSOP312.., 314.. [package=THT]
  Part1 = Arduino Uno (Rev3)

nets:
  GND: IR1.GND, Part1.GND
  N1: IR1.Vs, Part1.5V
  N2: IR1.Data, Part1.D11_PWM/MOSI
