# Fritzing sketch ArduinoI2C (saved by Fritzing 0.9.3b)

parts:
  Part1 = Arduino Nano (Rev3.0)
  Part2 = Arduino Uno (Rev3)

nets:
  GND: Part1.GND, Part2.GND
  N1: Part1.A5, Part2.A5/SCL
  N2: Part1.A4, Part2.A4/SDA
