# Fritzing sketch Sketch (saved by Fritzing 0.9.3b)
breadboards: 1

parts:
  R1 = TRIMPOT [package=3386u]
  Part1 = Arduino Uno (Rev3)

nets:
  N1: R1.CCW, Part1.5V
  N2: R1.WIPER, Part1.A0
  N3: R1.CW, Part1.GND
